// Digital circuit HW1-2-BIT.dig as structural Verilog
module HW1_2_BIT (
  input  A_0,
  input  A_1,
  input  B_0,
  input  B_1,
  output P_0,
  output P_1,
  output P_2,
  output P_3
);

  wire and_2_out, and_3_out, and_4_out, and_5_out;

  and and_1 (P_0, A_0, B_0);
  and and_2 (and_2_out, A_0, B_1);
  and and_3 (and_3_out, A_1, B_0);
  and and_4 (and_4_out, A_1, B_0);
  and and_5 (and_5_out, A_0, B_1);
  or or_1 (P_1, and_2_out, and_3_out);
  and and_6 (P_3, A_1, B_1);
  or or_2 (P_2, and_4_out, and_5_out);
endmodule
