// Digital circuit HW1_4-BIT.dig as structural Verilog
module HW1_4_BIT (
  input  A_0,
  input  B_0,
  input  C_in,
  input  A_1,
  input  B_1,
  input  A_2,
  input  B_2,
  input  A_3,
  input  B_3,
  output S_0,
  output S_1,
  output S_2,
  output C_out,
  output S_3
);

  wire and_1_out, and_2_out, and_3_out, and_4_out, and_5_out, and_6_out, and_7_out, and_8_out, and_9_out,
       and_10_out, and_11_out, and_12_out, xor_1_out, xor_3_out, xor_5_out, xor_7_out;

  xor xor_1 (xor_1_out, A_0, B_0);
  // XOr xor_2 has open pins: In_1=xor_1_out, In_2=C_in, out=open
  and and_1 (and_1_out, A_0, B_0);
  and and_2 (and_2_out, B_0, C_in);
  and and_3 (and_3_out, A_0, C_in);
  or or_1 (S_0, and_1_out, and_2_out, and_3_out);
  xor xor_3 (xor_3_out, A_1, B_1);
  // XOr xor_4 has open pins: In_1=xor_3_out, In_2=S_0, out=open
  and and_4 (and_4_out, A_1, B_1);
  and and_5 (and_5_out, B_1, S_0);
  and and_6 (and_6_out, A_1, S_0);
  or or_2 (S_1, and_4_out, and_5_out, and_6_out);
  xor xor_5 (xor_5_out, A_2, B_2);
  // XOr xor_6 has open pins: In_1=xor_5_out, In_2=S_1, out=open
  and and_7 (and_7_out, A_2, B_2);
  and and_8 (and_8_out, B_2, S_1);
  and and_9 (and_9_out, A_2, S_1);
  or or_3 (S_2, and_7_out, and_8_out, and_9_out);
  xor xor_7 (xor_7_out, A_3, B_3);
  // XOr xor_8 has open pins: In_1=xor_7_out, In_2=S_2, out=open
  and and_10 (and_10_out, A_3, B_3);
  and and_11 (and_11_out, B_3, S_2);
  and and_12 (and_12_out, A_3, S_2);
  or or_4 (C_out, and_10_out, and_11_out, and_12_out);

  assign S_3 = C_out;
endmodule
